# Fritzing sketch Sensor (saved by Fritzing 1.0.7)

parts:
  U1 = ESP8266 NodeMCU LoLin module
  C1 = Ceramic Capacitor [capacitance=100nF voltage=35V package="100 mil [THT, multilayer]"]
  R1 = Resistor [tolerance=±5% power=0.25W resistance=180k package=THT]
  OLED2 = OLED 128x64 I2C Monochrome Display GND-VDD
  S1 = Pushbutton [package="[THT]"]
  J1 = JST-B3P-VH [part_number=JST-SYP-3P package=THT]

nets:
  N1: U1.D1, OLED2.SCK
  N2: U1.D2, OLED2.SDA
  3V3: U1.3V3, OLED2.VDD
  GND: U1.GND, C1.0, OLED2.GND, S1.Pin_3, J1.pin1
  N3: U1.D7, S1.Pin_1
  N4: U1.VU, J1.pin3
  N5: U1.A0, C1.1, R1.Pin_1
  N6: R1.Pin_0, J1.pin2

notes:
  +5v
  Out 0.5...4.5V
  Common

custom parts:
  ESP8266 NodeMCU LoLin module: ESP8266 based NodeMCU
  OLED 128x64 I2C Monochrome Display GND-VDD: OLED 128x64 I2C Monochrome Display. Note: there are two variants of this part, this one is the GND VDD SCK SDA variant. The other is VDD GND SCK SDA. Make sure you select the part that matches your module as using the incorrect part will probably destroy your module! In addition the mounting holes are marked on silkscreen but not by default drilled. If you want drilled mounting holes, copy a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
